// Logisim project 4-BIT_ALU.circ as structural Verilog: 1 circuit, main circuit main
module main (
  input  Cin,
  input  S2,
  input  S1,
  input  S0,
  input  A1,
  input  B1,
  input  A2,
  input  B2,
  input  A3,
  input  B3,
  input  A4,
  input  B4,
  output f1,
  output f2,
  output f3,
  output f4,
  output Cout
);

  wire adder_1_cout, adder_2_cout, adder_3_cout, adder_4_cout, and_1_out, and_2_out, and_3_out, and_4_out,
       and_5_out, and_6_out, and_7_out, and_8_out, and_9_out, and_10_out, and_11_out, and_12_out, and_13_out,
       and_14_out, and_15_out, and_16_out, and_17_out, and_18_out, and_19_out, and_20_out, and_21_out,
       and_22_out, not_1_out, not_2_out, not_3_out, not_4_out, not_5_out, not_6_out, not_7_out, or_1_out,
       or_2_out, or_3_out, or_4_out, or_5_out, or_6_out, or_7_out, or_8_out;

  not not_1 (not_1_out, S2);
  not not_2 (not_2_out, S0);
  not not_3 (not_3_out, B1);
  not not_4 (not_4_out, B2);
  not not_5 (not_5_out, B3);
  not not_6 (not_6_out, B4);
  not not_7 (not_7_out, S1);
  and and_1 (and_1_out, not_2_out, S1, S2);
  and and_2 (and_2_out, not_2_out, not_7_out, S2);
  and and_3 (and_3_out, and_2_out, B1);
  and and_4 (and_4_out, and_1_out, not_3_out);
  and and_5 (and_5_out, B1, S0);
  and and_6 (and_6_out, not_3_out, S1);
  and and_7 (and_7_out, and_2_out, B2);
  and and_8 (and_8_out, and_1_out, not_4_out);
  and and_9 (and_9_out, B2, S0);
  and and_10 (and_10_out, not_4_out, S1);
  and and_11 (and_11_out, and_2_out, B3);
  and and_12 (and_12_out, and_1_out, not_5_out);
  and and_13 (and_13_out, B3, S0);
  and and_14 (and_14_out, not_5_out, S1);
  and and_15 (and_15_out, and_2_out, B4);
  and and_16 (and_16_out, and_1_out, not_6_out);
  and and_17 (and_17_out, B4, S0);
  and and_18 (and_18_out, not_6_out, S1);
  or or_1 (or_1_out, and_3_out, and_4_out, A1);
  or or_2 (or_2_out, and_5_out, and_6_out);
  or or_3 (or_3_out, and_7_out, and_8_out, A2);
  or or_4 (or_4_out, and_9_out, and_10_out);
  or or_5 (or_5_out, and_11_out, and_12_out, A3);
  or or_6 (or_6_out, and_13_out, and_14_out);
  or or_7 (or_7_out, and_15_out, and_16_out, A4);
  or or_8 (or_8_out, and_17_out, and_18_out);
  and and_19 (and_19_out, not_1_out, Cin);
  Adder #(.width(1)) adder_1 (.a(or_1_out), .b(or_2_out), .out(f1), .cin(and_19_out), .cout(adder_1_cout));
  and and_20 (and_20_out, not_1_out, adder_1_cout);
  Adder #(.width(1)) adder_2 (.a(or_3_out), .b(or_4_out), .out(f2), .cin(and_20_out), .cout(adder_2_cout));
  and and_21 (and_21_out, not_1_out, adder_2_cout);
  Adder #(.width(1)) adder_3 (.a(or_5_out), .b(or_6_out), .out(f3), .cin(and_21_out), .cout(adder_3_cout));
  and and_22 (and_22_out, not_1_out, adder_3_cout);
  Adder #(.width(1)) adder_4 (.a(or_7_out), .b(or_8_out), .out(f4), .cin(and_22_out), .cout(adder_4_cout));
  and and_23 (Cout, not_1_out, adder_4_cout);
endmodule
