// Logisim project 4-bit_multiplier.circ as structural Verilog: 1 circuit, main circuit main
module main (
  input  B3,
  input  B2,
  input  B1,
  input  Bo,
  input  Ao,
  input  in_6,
  input  A1,
  input  A2,
  input  A3,
  output out_10,
  output out_11,
  output out_12,
  output out_13,
  output out_14,
  output out_15,
  output out_16,
  output out_17
);

  wire [2:0] and_12_out;
  wire [3:0] adder_1_cout, adder_2_cout, and_13_out, and_14_out, and_15_out;

  and and_1 (and_14_out[3], A2, B3);
  and and_2 (and_15_out[3], A3, B3);
  and and_3 (and_12_out[2], Ao, B3);
  buf and_4 (and_13_out[3], A1);  // AND_Gate
  and and_5 (and_15_out[2], A3, B2);
  and and_6 (and_13_out[2], A1, B2);
  and and_7 (and_14_out[2], A2, B2);
  and and_8 (and_12_out[1], Ao, B2);
  and and_9 (and_13_out[1], A1, B1);
  and and_10 (and_14_out[1], A2, B1);
  and and_11 (and_15_out[1], A3, B1);
  and and_12 (and_12_out[0], Ao, B1);
  and and_13 (and_13_out[0], A1, Bo);
  and and_14 (and_14_out[0], A2, Bo);
  and and_15 (and_15_out[0], A3, Bo);
  and and_16 (out_17, Ao, Bo);
  Adder #(.width(4)) adder_1 (
    .a({in_6, and_12_out}), .b(and_13_out), .out({adder_1_cout[2:0], out_16}), .cout(adder_1_cout[3]));  // open: cin
  Adder #(.width(4)) adder_2 (
    .a(adder_1_cout), .b(and_14_out), .out({adder_2_cout[2:0], out_15}), .cout(adder_2_cout[3]));  // open: cin
  Adder #(.width(4)) adder_3 (
    .a(adder_2_cout), .b(and_15_out), .out({out_11, out_12, out_13, out_14}), .cout(out_10));  // open: cin
endmodule
