// Logisim project cls1.circ as structural Verilog: 1 circuit, main circuit main
module main (
  input  A,
  input  in_2,
  input  B,
  input  in_4,
  input  C,
  input  in_6,
  input  in_7,
  input  in_8,
  input  in_9,
  output S0,
  output S3,
  output C3,
  output S1,
  output S2
);

  wire and_1_out, and_2_out, and_3_out, and_4_out, and_5_out, and_6_out, and_7_out, and_8_out, or_1_out,
       or_2_out, or_3_out, xor_1_out, xor_2_out, xor_3_out, xor_7_out;

  and and_1 (and_1_out, B, A);
  xor xor_1 (xor_1_out, A, B);
  xor xor_2 (xor_2_out, in_6, in_7);
  and and_2 (and_2_out, in_7, in_6);
  xor xor_3 (xor_3_out, in_8, in_9);
  and and_3 (and_3_out, in_9, in_8);
  xor xor_4 (S0, xor_1_out, C);
  and and_4 (and_4_out, xor_1_out, C);
  xor xor_5 (S1, xor_2_out, or_1_out);
  and and_5 (and_5_out, xor_2_out, or_1_out);
  xor xor_6 (S2, xor_3_out, or_2_out);
  and and_6 (and_6_out, xor_3_out, or_2_out);
  or or_1 (or_1_out, and_4_out, and_1_out);
  or or_2 (or_2_out, and_5_out, and_2_out);
  or or_3 (or_3_out, and_6_out, and_3_out);
  xor xor_7 (xor_7_out, in_2, in_4);
  and and_7 (and_7_out, in_4, in_2);
  xor xor_8 (S3, xor_7_out, or_3_out);
  and and_8 (and_8_out, xor_7_out, or_3_out);
  or or_4 (C3, and_8_out, and_7_out);
endmodule
